// Digital circuit state.dig as structural Verilog
module state (
  input  [15:0] Lookup,
  input  [15:0] Shift_direction,
  input  from_q,
  input  Activating,
  output SHL,
  output SHR,
  output On,
  output On_2,
  output On_3,
  output On_4,
  output On_5,
  output On_6,
  output On_7,
  output On_8,
  output On_9,
  output On_10,
  output On_11,
  output On_12,
  output On_13,
  output On_14,
  output On_15,
  output On_16
);

  wire Active_value, Am_q_value, and_1_out, driver_1_out, not_1_out, not_2_out;

  not not_1 (not_1_out, Activating);
  flipflop Am_q (.Data(from_q), .Write(not_1_out), .Value(Am_q_value));
  and and_1 (and_1_out, Shift_direction[0], Lookup[0]);
  flipflop Active (.Data(Am_q_value), .Write(Activating), .Value(Active_value));
  not not_2 (not_2_out, and_1_out);
  assign driver_1_out = Activating ? Active_value : 1'bz;  // Driver driver_1
  assign SHL = driver_1_out ? and_1_out : 1'bz;  // Driver driver_2
  assign SHR = driver_1_out ? not_2_out : 1'bz;  // Driver driver_3
  assign {On_16, On_15, On_14, On_13, On_12, On_11, On_10, On_9, On_8, On_7, On_6, On_5, On_4, On_3, On_2, On} = driver_1_out ? Lookup : 16'bz;  // Driver driver_4
  // Pins of 1 and 16 bits meet at Lookup
  // Pins of 1 and 16 bits meet at Shift_direction

  // Notes on the sheet:
  //   Lookup: 16 bits, each corresponding to one tape symbol
  //   Shift_direction: 0 for R, 1 for L
  //   from_q: 1 if the current q is indicating that this is q'
  //   Activating: 1 when activated should be updated
  //   Phase 1: not Activating
  //   Send out all info
  //   Update Am q'
  //   Phase 2: Activating
  //   Stop writing to Am q'
  //   Stop sending any info
  //   Update Active
endmodule
