// Digital circuit testing.dig as structural Verilog
module testing (
  input  clk
);

  wire g0, t, t3, undriven, undriven_2, undriven_3, undriven_4, undriven_5, undriven_6;

  // start start_1: pin names not known; wires that end beside it: t, clk
  // state #(.generic("// shift := 0b0011 << 4 + 0b0000 << 4 + 0b0000 << 4 + 0b0000; //")) testing: pin names not known; wires that end beside it: 16'h2000, g0, g0, g0, g0, g0, g0, g0, g0, g0, g0, g0, g0, g0
  // state #(.generic("shift := 0x3000;")) testing2: pin names not known; wires that end beside it: g0, clk, 16'h400, t3
  // state #(.generic("shift := 0x3000;")) testing3: pin names not known; wires that end beside it: t3, clk, 16'h10, t
  LED led_1 (.in(undriven));
  LED led_2 (.in(undriven_2));
  LED led_3 (.in(undriven_3));
  LED led_4 (.in(undriven_4));
  LED led_5 (.in(undriven_5));
  LED led_6 (.in(undriven_6));

  // Other names for the same wires on the sheet: t2 = g0
endmodule
